// Logisim project RISC_V_CPU.circ as structural Verilog: 2 circuits, main circuit CPU
module CPU (
);

  Program_Counter program_counter_1 ();  // open: out_5, in_4, in_3, in_2, in_1
endmodule

module Program_Counter (
  input  [31:0] in_1,
  input  in_2,
  input  in_3,
  input  in_4,
  output [31:0] out_5
);

  Counter #(.width(32), .max('hffffffff)) counter_1 (
    .clr(in_2), .load(in_3), .clk(in_4), .D(in_1), .Q(out_5));  // open: up, count, carry

  // Other names for the same wires on the sheet: ADDR_IN[31:0] = in_1; ADDR_OUT[31:0] = out_5
endmodule
